// Logisim project 74LS173.circ as structural Verilog: 1 circuit, main circuit TTL74173
module TTL74173 (
  input  D0,
  input  IE1,
  input  D1,
  input  IE2,
  input  D2,
  input  VCC,
  input  GND,
  input  D3,
  input  CP,
  input  MR,
  input  OE1,
  input  OE2,
  output Q0,
  output Q1,
  output Q2,
  output Q3
);

  wire multiplexer_1_out, multiplexer_2_out, multiplexer_3_out, multiplexer_4_out, n74175_1_pin1,
       n74175_1_pin2, n74175_1_pin7, n74175_1_pin10, n74175_1_pin15, nor_1_out, nor_2_out;

  nor nor_1 (nor_1_out, IE1, IE2);
  Multiplexer multiplexer_1 (.in0(n74175_1_pin2), .in1(D0), .out(multiplexer_1_out), .sel(nor_1_out));
  Multiplexer multiplexer_2 (.in0(n74175_1_pin7), .in1(D1), .out(multiplexer_2_out), .sel(nor_1_out));
  Multiplexer multiplexer_3 (.in0(n74175_1_pin10), .in1(D2), .out(multiplexer_3_out), .sel(nor_1_out));
  Multiplexer multiplexer_4 (.in0(n74175_1_pin15), .in1(D3), .out(multiplexer_4_out), .sel(nor_1_out));
  _74175 u_74175_1 (
    .pin1(n74175_1_pin1), .pin2(n74175_1_pin2), .pin4(multiplexer_1_out), .pin5(multiplexer_2_out),
    .pin7(n74175_1_pin7), .pin15(n74175_1_pin15), .pin13(multiplexer_4_out), .pin12(multiplexer_3_out),
    .pin10(n74175_1_pin10), .pin9(CP));  // open: pin3, pin6, pin14, pin11
  not not_1 (n74175_1_pin1, MR);
  nor nor_2 (nor_2_out, OE1, OE2);
  assign Q0 = nor_2_out ? n74175_1_pin2 : 1'bz;  // Controlled_Buffer controlled_buffer_1
  assign Q1 = nor_2_out ? n74175_1_pin7 : 1'bz;  // Controlled_Buffer controlled_buffer_2
  assign Q2 = nor_2_out ? n74175_1_pin10 : 1'bz;  // Controlled_Buffer controlled_buffer_3
  assign Q3 = nor_2_out ? n74175_1_pin15 : 1'bz;  // Controlled_Buffer controlled_buffer_4

  // Notes on the sheet:
  //   74LS173
  //   Made by Acrilic
endmodule
